// Logisim project 32Bits_Computer_FB.circ as structural Verilog: 12 circuits, main circuit CPU
// Custom 32Bits CPU
module CPU (
);

  wire alu_1_zero, and_2_out, clock_1_out, comparator_1_eq, comparator_2_lt, controlunit_1_alu_src,
       controlunit_1_branch, controlunit_1_mem_read, controlunit_1_mem_to_reg, controlunit_1_mem_write,
       controlunit_1_reg_write, xor_1_out;
  wire [1:0] and_1_out;
  wire [3:0] controlunit_1_alu_control;
  wire [7:0] alu_1_alu_result_2;
  wire [31:0] adder_1_out, adder_2_out, datamemorymapped_1_read_data, datamemorymapped_1_row0,
       datamemorymapped_1_row1, datamemorymapped_1_row2, datamemorymapped_1_row3, datamemorymapped_1_row4,
       datamemorymapped_1_row5, datamemorymapped_1_row6, datamemorymapped_1_row7, datamemorymapped_1_row8,
       datamemorymapped_1_row9, datamemorymapped_1_row10, datamemorymapped_1_row11, datamemorymapped_1_row12,
       datamemorymapped_1_row13, datamemorymapped_1_row14, datamemorymapped_1_row15,
       immediatehandling_1_imm32, immediatehandling_1_imm_shifted, instructionmemory_1_instruction,
       multiplexers_1_alu_operand2, multiplexers_1_next_pc, multiplexers_1_write_data, programcounter_1_pc,
       register_1_q, registerfile_1_read_data1, registerfile_1_read_data2;
  wire [31:8] alu_1_alu_result;

  Clock clock_1 (.out(clock_1_out));
  // Probe on registerfile_1_read_data2
  // Probe on registerfile_1_read_data2
  // Probe on programcounter_1_pc
  ProgramCounter programcounter_1 (.next_pc(multiplexers_1_next_pc), .clk(clock_1_out), .pc(programcounter_1_pc));
  Adder #(.width(32)) adder_1 (.a(programcounter_1_pc), .b(32'h1), .out(adder_1_out));  // open: cin, cout
  DataMemoryMapped datamemorymapped_1 (
    .write_data(registerfile_1_read_data2), .mem_write(controlunit_1_mem_write),
    .mem_read(controlunit_1_mem_read), .clk(clock_1_out), .address({alu_1_alu_result, alu_1_alu_result_2}),
    .read_data(datamemorymapped_1_read_data), .row0(datamemorymapped_1_row0), .row1(datamemorymapped_1_row1),
    .row2(datamemorymapped_1_row2), .row3(datamemorymapped_1_row3), .row4(datamemorymapped_1_row4),
    .row5(datamemorymapped_1_row5), .row6(datamemorymapped_1_row6), .row7(datamemorymapped_1_row7),
    .row8(datamemorymapped_1_row8), .row9(datamemorymapped_1_row9), .row10(datamemorymapped_1_row10),
    .row11(datamemorymapped_1_row11), .row12(datamemorymapped_1_row12), .row13(datamemorymapped_1_row13),
    .row14(datamemorymapped_1_row14), .row15(datamemorymapped_1_row15));
  DotMatrix #(.inputtype("row"), .matrixcols(32), .matrixrows(16)) dotmatrix_1 (
    .row0(datamemorymapped_1_row0), .row1(datamemorymapped_1_row1), .row2(datamemorymapped_1_row2),
    .row3(datamemorymapped_1_row3), .row4(datamemorymapped_1_row4), .row5(datamemorymapped_1_row5),
    .row6(datamemorymapped_1_row6), .row7(datamemorymapped_1_row7), .row8(datamemorymapped_1_row8),
    .row9(datamemorymapped_1_row9), .row10(datamemorymapped_1_row10), .row11(datamemorymapped_1_row11),
    .row12(datamemorymapped_1_row12), .row13(datamemorymapped_1_row13), .row14(datamemorymapped_1_row14),
    .row15(datamemorymapped_1_row15));
  // Probe on instructionmemory_1_instruction[20:16]
  InstructionMemory instructionmemory_1 (.address(programcounter_1_pc), .instruction(instructionmemory_1_instruction));
  // Probe on datamemorymapped_1_read_data
  // Probe on instructionmemory_1_instruction[31:26]
  // Probe on controlunit_1_reg_write
  // Probe on {{15{1'b0}}, instructionmemory_1_instruction[16:0]}
  // Probe on instructionmemory_1_instruction[31:26]
  // Probe on multiplexers_1_next_pc
  // Probe on controlunit_1_mem_write
  // Probe on controlunit_1_mem_read
  Comparator #(.width(6)) comparator_1 (
    .a(instructionmemory_1_instruction[31:26]), .b(6'b000101), .eq(comparator_1_eq));  // open: gt, lt
  // Probe on comparator_1_eq
  // Probe on immediatehandling_1_imm_shifted
  // Probe on immediatehandling_1_imm32
  ImmediateHandling immediatehandling_1 (
    .imm16(instructionmemory_1_instruction[15:0]), .imm32(immediatehandling_1_imm32),
    .imm_shifted(immediatehandling_1_imm_shifted));
  RegisterFile registerfile_1 (
    .clk(clock_1_out), .write_data(multiplexers_1_write_data),
    .read_reg1(instructionmemory_1_instruction[18:16]), .reg_write(controlunit_1_reg_write),
    .write_reg(instructionmemory_1_instruction[23:21]), .read_reg2(instructionmemory_1_instruction[23:21]),
    .read_data1(registerfile_1_read_data1), .read_data2(registerfile_1_read_data2));
  ControlUnit controlunit_1 (
    .Opcode(instructionmemory_1_instruction[31:26]), .alu_control(controlunit_1_alu_control),
    .jump(and_1_out[1]), .branch(controlunit_1_branch), .mem_write(controlunit_1_mem_write),
    .mem_read(controlunit_1_mem_read), .mem_to_reg(controlunit_1_mem_to_reg),
    .alu_src(controlunit_1_alu_src), .reg_write(controlunit_1_reg_write));
  xor xor_1 (xor_1_out, alu_1_zero, comparator_1_eq);
  // Probe on xor_1_out
  // Probe on controlunit_1_mem_to_reg
  Adder #(.width(32)) adder_2 (
    .a(adder_1_out), .b(immediatehandling_1_imm_shifted), .out(adder_2_out));  // open: cin, cout
  and and_1 (and_1_out[0], controlunit_1_branch, xor_1_out);
  // Probe on alu_1_alu_result_2
  Comparator comparator_2 (.a(8'hef), .b(alu_1_alu_result_2), .lt(comparator_2_lt));  // open: gt, eq
  // Probe on controlunit_1_alu_control
  // Probe on multiplexers_1_alu_operand2
  // Probe on registerfile_1_read_data1
  // Probe on adder_1_out
  // Probe on and_1_out
  and and_2 (and_2_out, controlunit_1_mem_write, comparator_2_lt);
  // Probe on registerfile_1_read_data2
  Register #(.width(32)) register_1 (
    .D(registerfile_1_read_data2), .en(and_2_out), .clk(clock_1_out), .Q(register_1_q), .clr(1'b0));
  ALU alu_1 (
    .operand1(registerfile_1_read_data1), .operand2(multiplexers_1_alu_operand2),
    .aliu_control(controlunit_1_alu_control), .alu_result({alu_1_alu_result, alu_1_alu_result_2}),
    .zero(alu_1_zero));  // open: Carry, Negative, BorrowOut, Overflow
  Multiplexers multiplexers_1 (
    .reg_data2(registerfile_1_read_data2), .imm32(immediatehandling_1_imm32),
    .alu_src(controlunit_1_alu_src), .alu_result({alu_1_alu_result, alu_1_alu_result_2}),
    .mem_data(datamemorymapped_1_read_data), .mem_read(controlunit_1_mem_read),
    .mem_to_reg(controlunit_1_mem_to_reg), .pc_plus_1(adder_1_out), .branch_target(adder_2_out),
    .jump_target({{15{1'b0}}, instructionmemory_1_instruction[16:0]}), .pc_src(and_1_out),
    .alu_operand2(multiplexers_1_alu_operand2), .write_data(multiplexers_1_write_data),
    .next_pc(multiplexers_1_next_pc));
  LED led_1 (.in(register_1_q[7]));
  LED led_2 (.in(register_1_q[6]));
  // Probe on registerfile_1_read_data1
  // Probe on registerfile_1_read_data2
  // Probe on datamemorymapped_1_read_data
  // Probe on {alu_1_alu_result, alu_1_alu_result_2}
  // Probe on adder_2_out
  // Probe on {alu_1_alu_result, alu_1_alu_result_2}
  // Probe on register_1_q
  LED led_3 (.in(register_1_q[5]));
  LED led_4 (.in(register_1_q[4]));
  LED led_5 (.in(register_1_q[3]));
  LED led_6 (.in(register_1_q[2]));
  LED led_7 (.in(register_1_q[1]));
  LED led_8 (.in(register_1_q[0]));

  // Notes on the sheet:
  //   branch_taken
endmodule

module RegisterFile (
  input  clk,
  input  [31:0] write_data,
  input  [2:0] read_reg1,
  input  reg_write,
  input  [2:0] write_reg,
  input  [2:0] read_reg2,
  output [31:0] read_data1,
  output [31:0] read_data2
);

  wire decoder_1_out0, decoder_1_out1, decoder_1_out2, decoder_1_out3, decoder_1_out4, decoder_1_out5,
       decoder_1_out6, decoder_1_out7;
  wire [31:0] R0_q, R1_q, R2_q, R3_q, R4_q, R5_q, R6_q, R7_q;

  Decoder #(.select(3)) decoder_1 (
    .out0(decoder_1_out0), .out1(decoder_1_out1), .out2(decoder_1_out2), .out3(decoder_1_out3),
    .out4(decoder_1_out4), .out5(decoder_1_out5), .out6(decoder_1_out6), .out7(decoder_1_out7),
    .sel(write_reg), .en(reg_write));
  Register #(.width(32)) R0 (.D(write_data), .en(decoder_1_out0), .clk(clk), .Q(R0_q), .clr(1'b0));
  Register #(.width(32)) R1 (.D(write_data), .en(decoder_1_out1), .clk(clk), .Q(R1_q), .clr(1'b0));
  Register #(.width(32)) R2 (.D(write_data), .en(decoder_1_out2), .clk(clk), .Q(R2_q), .clr(1'b0));
  Register #(.width(32)) R3 (.D(write_data), .en(decoder_1_out3), .clk(clk), .Q(R3_q), .clr(1'b0));
  Register #(.width(32)) R4 (.D(write_data), .en(decoder_1_out4), .clk(clk), .Q(R4_q), .clr(1'b0));
  Register #(.width(32)) R5 (.D(write_data), .en(decoder_1_out5), .clk(clk), .Q(R5_q), .clr(1'b0));
  Register #(.width(32)) R6 (.D(write_data), .en(decoder_1_out6), .clk(clk), .Q(R6_q), .clr(1'b0));
  Register #(.width(32)) R7 (.D(write_data), .en(decoder_1_out7), .clk(clk), .Q(R7_q), .clr(1'b0));
  Multiplexer #(.select(3), .width(32)) multiplexer_1 (
    .in0(R0_q), .in1(R1_q), .in2(R2_q), .in3(R3_q), .in4(R4_q), .in5(R5_q), .in6(R6_q), .in7(R7_q),
    .out(read_data1), .sel(read_reg1));
  Multiplexer #(.select(3), .width(32)) multiplexer_2 (
    .in0(R0_q), .in1(R1_q), .in2(R2_q), .in3(R3_q), .in4(R4_q), .in5(R5_q), .in6(R6_q), .in7(R7_q),
    .out(read_data2), .sel(read_reg2));

  // Notes on the sheet:
  //   reg_write: initial=0x1
endmodule

module ALU (
  input  [31:0] operand1,
  input  [31:0] operand2,
  input  [3:0] aliu_control,
  output Carry,
  output Negative,
  output BorrowOut,
  output Overflow,
  output [31:0] alu_result,
  output zero
);

  wire xor_2_out, xor_3_out;
  wire [31:0] adder_1_out, and_1_out, not_1_out, or_1_out, shifter_1_out, shifter_2_out, subtractor_1_out,
       xor_1_out;

  Adder #(.width(32)) adder_1 (.a(operand1), .b(operand2), .out(adder_1_out), .cout(Carry));  // open: cin
  Subtractor #(.width(32)) subtractor_1 (
    .a(operand1), .b(operand2), .out(subtractor_1_out), .bout(BorrowOut));  // open: bin
  assign and_1_out = operand1 & operand2;  // AND_Gate and_1, 32 bits wide
  assign or_1_out = operand1 | operand2;  // OR_Gate or_1, 32 bits wide
  assign not_1_out = ~operand1;  // NOT_Gate not_1, 32 bits wide
  Shifter #(.width(32)) shifter_1 (.in(operand1), .\dist (5'b00001), .out(shifter_1_out));
  Shifter #(.shift("lr"), .width(32)) shifter_2 (.in(operand1), .\dist (5'b00001), .out(shifter_2_out));
  assign xor_1_out = operand1 ^ operand2;  // XOR_Gate xor_1, 32 bits wide
  Multiplexer #(.select(4), .width(32)) multiplexer_1 (
    .in0(adder_1_out), .in1(subtractor_1_out), .in2(and_1_out), .in3(or_1_out), .in4(not_1_out),
    .in5(shifter_1_out), .in6(shifter_2_out), .in7(xor_1_out), .out(alu_result), .sel(aliu_control));  // open: in8, in9, in10, in11, in12, in13, in14, in15
  Comparator #(.width(32)) comparator_1 (.a(alu_result), .b({32{1'b0}}), .eq(zero));  // open: gt, lt
  xor xor_2 (xor_2_out, alu_result[31], operand1[31]);
  and and_2 (Overflow, xor_2_out, xor_3_out);
  xor xor_3 (xor_3_out, operand2[31], operand1[31]);

  assign Negative = alu_result[31];
endmodule

module ControlUnit (
  input  [5:0] Opcode,
  output [3:0] alu_control,
  output jump,
  output branch,
  output mem_write,
  output mem_read,
  output mem_to_reg,
  output alu_src,
  output reg_write
);

  wire [0:0] ControlSignalLookup_data;

  ROM #(.addrWidth(6), .dataWidth(12)) ControlSignalLookup (
    .addr(Opcode),
    .data({alu_control, jump, branch, mem_write, mem_read, mem_to_reg, alu_src, reg_write, ControlSignalLookup_data[0]}));

  // Notes on the sheet:
  //   contents of ControlSignalLookup (hex, n*v repeats v):
  //   0 6 80 140 502 140 0 0 2 102 202 302 702 402 602 0 1e 24
endmodule

module InstructionMemory (
  input  [31:0] address,
  output [31:0] instruction
);

  ROM #(.addrWidth(10), .dataWidth(32)) rom_1 (.addr(address[9:0]), .data(instruction));

  // Notes on the sheet:
  //   contents of rom_1 (hex, n*v repeats v):
  //   420ffff 442000fe 4200018 440003c 4600004 480000e 4a00004 4c0000a 4e00011 10630000 10840000 10a50000
  //   10c60000 10e70000 10630000 10840000 10a50000 10c60000 10e70000 10630000 10840000 10a50000 10c60000
  //   10e70000 10630000 10840000 10a50000 10c60000 10e70000 10630000 10840000 10a50000 10c60000 10e70000
  //   10630000 10840000 10a50000 10c60000 10e70000 10630000 10840000 10a50000 10c60000 10e70000 10630000
  //   10840000 10a50000 10c60000 10e70000 10630000 10840000 10a50000 10c60000 10e70000 10630000 10840000
  //   10a50000 10c60000 10e70000 10630000 10840000 10a50000 10c60000 10e70000 10630000 10840000 10a50000
  //   10c60000 10e70000 10630000 10840000 10a50000 10c60000 10e70000 10630000 10840000 10a50000 10c60000
  //   10e70000 10630000 10840000 10a50000 10c60000 10e70000 10630000 10840000 10a50000 10c60000 10e70000
  //   10630000 10840000 10a50000 10c60000 10e70000 10630000 10840000 10a50000 10c60000 10e70000 10630000
  //   10840000 10a50000 10c60000 10e70000 10630000 10840000 10a50000 10c60000 10e70000 10630000 10840000
  //   10a50000 10c60000 10e70000 10630000 10840000 10a50000 10c60000 10e70000 10630000 10840000 10a50000
  //   10c60000 10e70000 442000f1 444000f2 446000f9 448000fa 44a000fb 44c000fc 44e000fd 10a50000 10e70000
  //   442000f1 444000f2 446000f9 448000fa 44a000fb 44c000fc 44e000fd 38a50000 38e70000 10210000 10420000
  //   38630000 38840000 38a50000 38c60000 38e70000 14e0ffe6 8000097 420ffff 442000fe 4200018 440003c
  //   4600004 480000e 4a00004 4c0000a 4e00011 10210000 10420000 10210000 10420000 10210000 10420000
  //   10210000 10420000 10210000 10420000 10210000 10420000 10210000 10420000 10210000 10420000 10210000
  //   10420000 10210000 10420000 10210000 10420000 10210000 10420000 10210000 10420000 10210000 10420000
  //   10210000 10420000 10210000 10420000 10210000 10420000 10210000 10420000 10210000 10420000 10210000
  //   10420000 10210000 10420000 10210000 10420000 10210000 10420000 442000f1 444000f2 446000f9 448000fa
  //   44a000fb 44c000fc 44e000fd 38a50000 38e70000 442000f1 444000f2 446000f9 448000fa 44a000fb 44c000fc
  //   44e000fd 10a50000 10e70000 38210000 38420000 10630000 10840000 10a50000 10c60000 10e70000 14e0ffe6
  //   8000002
endmodule

module ProgramCounter (
  input  [31:0] next_pc,
  input  clk,
  output [31:0] pc
);

  Register #(.width(32)) register_1 (.D(next_pc), .clk(clk), .Q(pc));  // open: en, clr
endmodule

module Multiplexers (
  input  [31:0] reg_data2,
  input  [31:0] imm32,
  input  alu_src,
  input  [31:0] alu_result,
  input  [31:0] mem_data,
  input  mem_read,
  input  mem_to_reg,
  input  [31:0] pc_plus_1,
  input  [31:0] branch_target,
  input  [31:0] jump_target,
  input  [1:0] pc_src,
  output [31:0] alu_operand2,
  output [31:0] write_data,
  output [31:0] next_pc
);

  wire [31:0] multiplexer_1_out;

  Multiplexer #(.width(32)) multiplexer_1 (.in0({32{1'b0}}), .in1(mem_data), .out(multiplexer_1_out), .sel(mem_read));
  Multiplexer #(.width(32)) multiplexer_2 (.in0(reg_data2), .in1(imm32), .out(alu_operand2), .sel(alu_src));
  Multiplexer #(.select(2), .width(32)) multiplexer_3 (
    .in0(pc_plus_1), .in1(branch_target), .in2(jump_target), .out(next_pc), .sel(pc_src));  // open: in3
  Multiplexer #(.width(32)) multiplexer_4 (
    .in0(alu_result), .in1(multiplexer_1_out), .out(write_data), .sel(mem_to_reg));

  // Notes on the sheet:
  //   ALU Source MUX
  //   Write-Back MUX
  //   PC Source MUX
endmodule

module SignExtender (
  input  [15:0] imm16,
  output [31:0] imm32
);


  assign imm32 = {{17{imm16[15]}}, imm16[14:0]};
endmodule

module DataMemory (
  input  [31:0] write_data,
  input  mem_write,
  input  mem_read,
  input  clk,
  input  [31:0] address,
  output [31:0] read_data
);

  RAM #(.dataWidth(32)) ram_1 (
    .addr(address[7:0]), .we(mem_write), .oe(mem_read), .clk(clk), .din(write_data), .dout(read_data));
endmodule

module ImmediateHandling (
  input  [15:0] imm16,
  output [31:0] imm32,
  output [31:0] imm_shifted
);

  SignExtender signextender_1 (.imm16(imm16), .imm32(imm32));
  Shifter #(.width(32)) shifter_1 (.in(imm32), .\dist (5'b00010));  // open: out

  assign imm_shifted = imm32;
endmodule

module FrameBuffer32x16 (
  input  [31:0] write_data,
  input  we,
  input  [3:0] addr,
  input  clk,
  output [31:0] row0,
  output [31:0] row1,
  output [31:0] row2,
  output [31:0] row3,
  output [31:0] row4,
  output [31:0] row5,
  output [31:0] row6,
  output [31:0] row7,
  output [31:0] read_data,
  output [31:0] row8,
  output [31:0] row9,
  output [31:0] row10,
  output [31:0] row11,
  output [31:0] row12,
  output [31:0] row13,
  output [31:0] row14,
  output [31:0] row15
);

  wire decoder_1_out0, decoder_1_out1, decoder_1_out2, decoder_1_out3, decoder_1_out4, decoder_1_out5,
       decoder_1_out6, decoder_1_out7, decoder_1_out8, decoder_1_out9, decoder_1_out10, decoder_1_out11,
       decoder_1_out12, decoder_1_out13, decoder_1_out14, decoder_1_out15;

  Decoder #(.select(4)) decoder_1 (
    .out0(decoder_1_out0), .out1(decoder_1_out1), .out2(decoder_1_out2), .out3(decoder_1_out3),
    .out4(decoder_1_out4), .out5(decoder_1_out5), .out6(decoder_1_out6), .out7(decoder_1_out7),
    .out8(decoder_1_out8), .out9(decoder_1_out9), .out10(decoder_1_out10), .out11(decoder_1_out11),
    .out12(decoder_1_out12), .out13(decoder_1_out13), .out14(decoder_1_out14), .out15(decoder_1_out15),
    .sel(addr), .en(we));
  Register #(.width(32)) FB0 (.D(write_data), .en(decoder_1_out0), .clk(clk), .Q(row0), .clr(1'b0));
  Register #(.width(32)) FB4 (.D(write_data), .en(decoder_1_out4), .clk(clk), .Q(row4), .clr(1'b0));
  Register #(.width(32)) FB8 (.D(write_data), .en(decoder_1_out8), .clk(clk), .Q(row8), .clr(1'b0));
  Register #(.width(32)) FB12 (.D(write_data), .en(decoder_1_out12), .clk(clk), .Q(row12), .clr(1'b0));
  Register #(.width(32)) FB1 (.D(write_data), .en(decoder_1_out1), .clk(clk), .Q(row1), .clr(1'b0));
  Register #(.width(32)) FB5 (.D(write_data), .en(decoder_1_out5), .clk(clk), .Q(row5), .clr(1'b0));
  Register #(.width(32)) FB9 (.D(write_data), .en(decoder_1_out9), .clk(clk), .Q(row9), .clr(1'b0));
  Register #(.width(32)) FB13 (.D(write_data), .en(decoder_1_out13), .clk(clk), .Q(row13), .clr(1'b0));
  Register #(.width(32)) FB2 (.D(write_data), .en(decoder_1_out2), .clk(clk), .Q(row2), .clr(1'b0));
  Register #(.width(32)) FB6 (.D(write_data), .en(decoder_1_out6), .clk(clk), .Q(row6), .clr(1'b0));
  Register #(.width(32)) FB10 (.D(write_data), .en(decoder_1_out10), .clk(clk), .Q(row10), .clr(1'b0));
  Register #(.width(32)) FB14 (.D(write_data), .en(decoder_1_out14), .clk(clk), .Q(row14), .clr(1'b0));
  Register #(.width(32)) FB3 (.D(write_data), .en(decoder_1_out3), .clk(clk), .Q(row3), .clr(1'b0));
  Register #(.width(32)) FB7 (.D(write_data), .en(decoder_1_out7), .clk(clk), .Q(row7), .clr(1'b0));
  Register #(.width(32)) FB11 (.D(write_data), .en(decoder_1_out11), .clk(clk), .Q(row11), .clr(1'b0));
  Register #(.width(32)) FB15 (.D(write_data), .en(decoder_1_out15), .clk(clk), .Q(row15), .clr(1'b0));
  Multiplexer #(.select(4), .width(32)) multiplexer_1 (
    .in0(row0), .in1(row1), .in2(row2), .in3(row3), .in4(row4), .in5(row5), .in6(row6), .in7(row7),
    .in8(row8), .in9(row9), .in10(row10), .in11(row11), .in12(row12), .in13(row13), .in14(row14),
    .in15(row15), .out(read_data), .sel(addr));
endmodule

module DataMemoryMapped (
  input  [31:0] write_data,
  input  mem_write,
  input  mem_read,
  input  clk,
  input  [31:0] address,
  output [31:0] read_data,
  output [31:0] row0,
  output [31:0] row1,
  output [31:0] row2,
  output [31:0] row3,
  output [31:0] row4,
  output [31:0] row5,
  output [31:0] row6,
  output [31:0] row7,
  output [31:0] row8,
  output [31:0] row9,
  output [31:0] row10,
  output [31:0] row11,
  output [31:0] row12,
  output [31:0] row13,
  output [31:0] row14,
  output [31:0] row15
);

  wire and_1_out, comparator_1_eq;
  wire [31:0] framebuffer32x16_1_read_data, ram_1_dout;

  Comparator #(.width(4)) comparator_1 (.a(address[7:4]), .b(4'b1111), .eq(comparator_1_eq));  // open: gt, lt
  and and_1 (and_1_out, comparator_1_eq, mem_write);
  RAM #(.dataWidth(32), .enables("line"), .misaligned("true")) ram_1 (
    .addr(address[7:0]), .we(mem_write), .clk(clk), .din(write_data), .dout(ram_1_dout));
  Multiplexer #(.width(32)) multiplexer_1 (
    .in0(ram_1_dout), .in1(framebuffer32x16_1_read_data), .out(read_data), .sel(comparator_1_eq));
  FrameBuffer32x16 framebuffer32x16_1 (
    .write_data(write_data), .we(and_1_out), .addr(address[3:0]), .clk(clk), .row0(row0), .row1(row1),
    .row2(row2), .row3(row3), .row4(row4), .row5(row5), .row6(row6), .row7(row7),
    .read_data(framebuffer32x16_1_read_data), .row8(row8), .row9(row9), .row10(row10), .row11(row11),
    .row12(row12), .row13(row13), .row14(row14), .row15(row15));
endmodule
